// Logisim project 1.Divisori di 3.circ as structural Verilog: 1 circuit, main circuit main
module main (
  input  x1,
  input  x2,
  input  x3,
  input  x4,
  output out_5
);

  wire and_1_out, and_2_out, and_3_out, and_4_out, and_5_out, and_6_out;

  and and_1 (and_1_out, ~x1, ~x2, ~x3, ~x4);  // AND_Gate
  and and_2 (and_2_out, x1, x2, ~x3, ~x4);  // AND_Gate
  and and_3 (and_3_out, x1, ~x2, ~x3, x4);  // AND_Gate
  and and_4 (and_4_out, ~x1, ~x2, x3, x4);  // AND_Gate
  and and_5 (and_5_out, x1, x2, x3, x4);
  and and_6 (and_6_out, ~x1, x2, x3, ~x4);  // AND_Gate
  or or_1 (out_5, and_1_out, and_2_out, and_3_out, and_4_out, and_5_out, and_6_out);
endmodule
