// Logisim project 3.a minore b.circ as structural Verilog: 1 circuit, main circuit main
module main (
  input  a1,
  input  a0,
  input  b1,
  input  b0,
  output out_5
);

  wire and_1_out, and_2_out, and_3_out;

  and and_1 (and_1_out, ~a1, ~a0, ~b1, b0);  // AND_Gate
  and and_2 (and_2_out, ~a1, b1);  // AND_Gate
  and and_3 (and_3_out, a1, ~a0, b1, b1);  // AND_Gate
  or or_1 (out_5, and_1_out, and_2_out, and_3_out);
endmodule
