// Logisim project ALU a 4 bit.circ as structural Verilog: 1 circuit
module circuit (
  input  OPTYPE__1,
  input  [1:0] OPTYPE__2__3,
  input  x3,
  input  x2,
  input  x1,
  input  x0,
  input  y3,
  input  y2,
  input  y,
  input  y0,
  output S0,
  output OVERFLOW,
  output S3,
  output S2,
  output S1
);

  wire and_1_out, and_2_out, and_3_out, and_4_out, and_5_out, and_6_out, and_7_out, and_8_out, and_9_out,
       and_10_out, and_11_out, and_12_out, and_13_out, and_14_out, and_15_out, and_16_out, not_1_out,
       not_2_out, not_3_out, not_4_out, or_1_out, or_2_out, or_3_out, or_4_out, or_6_out, or_7_out, or_8_out,
       xor_1_out, xor_2_out, xor_3_out, xor_4_out, xor_5_out, xor_6_out, xor_7_out, xor_8_out;

  xor xor_1 (xor_1_out, y0, OPTYPE__1);
  xor xor_2 (xor_2_out, y, OPTYPE__1);
  xor xor_3 (xor_3_out, OPTYPE__1, y2);
  xor xor_4 (xor_4_out, OPTYPE__1, y3);
  or or_1 (or_1_out, x3, or_8_out);
  and and_1 (and_1_out, x3, or_8_out);
  and and_2 (and_2_out, or_8_out, xor_4_out);
  and and_3 (and_3_out, or_8_out, x3);
  and and_4 (and_4_out, x3, xor_4_out);
  or or_2 (or_2_out, x0, OPTYPE__1);
  and and_5 (and_5_out, x0, OPTYPE__1);
  xor xor_5 (xor_5_out, OPTYPE__1, x0, xor_1_out);
  and and_6 (and_6_out, OPTYPE__1, xor_1_out);
  and and_7 (and_7_out, OPTYPE__1, x0);
  and and_8 (and_8_out, x0, xor_1_out);
  or or_3 (or_3_out, x1, or_6_out);
  and and_9 (and_9_out, x1, or_6_out);
  xor xor_6 (xor_6_out, or_6_out, x1, xor_2_out);
  and and_10 (and_10_out, or_6_out, xor_2_out);
  and and_11 (and_11_out, or_6_out, x1);
  and and_12 (and_12_out, x1, xor_2_out);
  or or_4 (or_4_out, x2, or_7_out);
  and and_13 (and_13_out, x2, or_7_out);
  not not_1 (not_1_out, or_7_out);
  xor xor_7 (xor_7_out, or_7_out, x2, xor_3_out);
  and and_14 (and_14_out, or_7_out, xor_3_out);
  and and_15 (and_15_out, or_7_out, x2);
  and and_16 (and_16_out, x2, xor_3_out);
  Multiplexer #(.select(2), .enable("false")) multiplexer_1 (
    .in0(or_1_out), .in1(and_1_out), .in2(xor_8_out), .in3(not_2_out), .out(S3), .sel(OPTYPE__2__3));
  not not_2 (not_2_out, or_8_out);
  xor xor_8 (xor_8_out, or_8_out, x3, xor_4_out);
  or or_5 (OVERFLOW, and_2_out, and_3_out, and_4_out);
  Multiplexer #(.select(2), .enable("false")) multiplexer_2 (
    .in0(or_2_out), .in1(and_5_out), .in2(xor_5_out), .in3(not_3_out), .out(S0), .sel(OPTYPE__2__3));
  not not_3 (not_3_out, OPTYPE__1);
  or or_6 (or_6_out, and_6_out, and_7_out, and_8_out);
  Multiplexer #(.select(2), .enable("false")) multiplexer_3 (
    .in0(or_3_out), .in1(and_9_out), .in2(xor_6_out), .in3(not_4_out), .out(S1), .sel(OPTYPE__2__3));
  not not_4 (not_4_out, or_6_out);
  or or_7 (or_7_out, and_10_out, and_11_out, and_12_out);
  Multiplexer #(.select(2), .enable("false")) multiplexer_4 (
    .in0(or_4_out), .in1(and_13_out), .in2(xor_7_out), .in3(not_1_out), .out(S2), .sel(OPTYPE__2__3));
  or or_8 (or_8_out, and_14_out, and_15_out, and_16_out);

  // Notes on the sheet:
  //   x
  //   y
  //   c
  //   x
  //   y
  //   c
  //   x
  //   y
  //   c
  //   x
  //   y
  //   c
endmodule
